# Fritzing sketch project2 (saved by Fritzing 0.9.1b)
breadboards: 1

parts:
  Part1 = Spark Core (v1.0)
  J2 = Basic Force Sensing Resistor (FSR) [package=THT]
  R1 = Resistor [package="0402 [SMD]"]
  Power_plug2 = Power plug
  J3 = Basic Servo

nets:
  N1: Part1.VIN, J3.pulse
  N2: Part1.3V3, R1.Pin_0
  N3: J2.pin_0, R1.Pin_1
  N4: J2.pin_1, Power_plug2.VCC

notes:
  Food dispenser
